// Logisim project Sinaleiro_das_3_ruas.circ as structural Verilog: 1 circuit, main circuit main
module main (
  input  A,
  input  B,
  input  C
);

  wire and_1_out, and_2_out, and_3_out, and_4_out, not_1_out, not_2_out, not_3_out, not_4_out, not_5_out,
       not_6_out, not_7_out, or_1_out, or_2_out;

  not not_1 (not_1_out, C);
  not not_2 (not_2_out, B);
  not not_3 (not_3_out, A);
  not not_4 (not_4_out, B);
  and and_1 (and_1_out, A, or_1_out);
  or or_1 (or_1_out, B, not_1_out);
  and and_2 (and_2_out, not_1_out, not_2_out);
  and and_3 (and_3_out, not_3_out, B);
  and and_4 (and_4_out, not_4_out, C);
  LED led_1 (.in(or_2_out));
  or or_2 (or_2_out, and_1_out, and_2_out);
  LED led_2 (.in(not_5_out));
  LED led_3 (.in(and_3_out));
  LED led_4 (.in(not_6_out));
  not not_5 (not_5_out, or_2_out);
  not not_6 (not_6_out, and_3_out);
  LED led_5 (.in(and_4_out));
  LED led_6 (.in(not_7_out));
  not not_7 (not_7_out, and_4_out);

  // Notes on the sheet:
  //   A
  //   B
  //   C
endmodule
